// Logisim project POTEC-25L-01-JC-KK.circ as structural Verilog: 8 circuits, main circuit Dekoder
module systematyczne_e (
  input  x3,
  input  x2,
  input  x1,
  input  x0,
  output out_5
);

  wire and_1_out, and_2_out, not_1_out, not_2_out;

  not not_1 (not_1_out, x2);
  not not_2 (not_2_out, x0);
  and and_1 (and_1_out, not_2_out, x1);
  and and_2 (and_2_out, not_1_out, not_2_out);
  or or_1 (out_5, and_1_out, and_2_out);
endmodule

module systematyczne_f (
  input  x3,
  input  x2,
  input  x1,
  input  x0,
  output f
);

  wire and_1_out, and_2_out, and_3_out, not_1_out, not_2_out;

  not not_1 (not_1_out, x1);
  not not_2 (not_2_out, x0);
  and and_1 (and_1_out, not_1_out, x2);
  and and_2 (and_2_out, x2, not_2_out);
  and and_3 (and_3_out, not_1_out, not_2_out);
  or or_1 (f, x3, and_1_out, and_2_out, and_3_out);
endmodule

module heurystyczne_g (
  input  x3,
  input  x2,
  input  x1,
  input  x0,
  output g
);

  wire and_1_out, and_2_out, and_3_out, not_1_out, not_2_out, not_3_out;

  not not_1 (not_1_out, x2);
  not not_2 (not_2_out, x1);
  not not_3 (not_3_out, x0);
  and and_1 (and_1_out, x1, not_1_out);
  and and_2 (and_2_out, x2, not_3_out);
  and and_3 (and_3_out, x2, not_2_out);
  or or_1 (g, x3, and_1_out, and_2_out, and_3_out);
endmodule

module heurystyczne_a (
  input  x3,
  input  x2,
  input  x1,
  input  x0,
  output a
);

  wire and_1_out, and_2_out, not_1_out, not_2_out;

  not not_1 (not_1_out, x2);
  not not_2 (not_2_out, x0);
  and and_1 (and_1_out, not_1_out, not_2_out);
  and and_2 (and_2_out, x2, x0);
  or or_1 (a, and_1_out, x3, x1, and_2_out);
endmodule

module Dekoder (
  input  x3,
  input  x2,
  input  x1,
  input  x0
);

  wire heurystyczne_a_1_a, heurystyczne_g_1_g, karnaugh_dla_0_pos_c_1_c, karnaugh_dla_0_pos_d_1_d,
       karnaugh_dla_1_sop_b_1_b, systematyczne_e_1_out_5, systematyczne_f_1_f;

  heurystyczne_a heurystyczne_a_1 (.x3(x3), .x2(x2), .x1(x1), .x0(x0), .a(heurystyczne_a_1_a));
  karnaugh_dla_1_SOP_b karnaugh_dla_1_sop_b_1 (.x3(x3), .x2(x2), .x1(x1), .x0(x0), .b(karnaugh_dla_1_sop_b_1_b));
  karnaugh_dla_0_POS_c karnaugh_dla_0_pos_c_1 (.x3(x3), .x2(x2), .x1(x1), .x0(x0), .c(karnaugh_dla_0_pos_c_1_c));
  karnaugh_dla_0_POS_d karnaugh_dla_0_pos_d_1 (.x3(x3), .x2(x2), .x1(x1), .x0(x0), .d(karnaugh_dla_0_pos_d_1_d));
  systematyczne_e systematyczne_e_1 (.x3(x3), .x2(x2), .x1(x1), .x0(x0), .out_5(systematyczne_e_1_out_5));
  systematyczne_f systematyczne_f_1 (.x3(x3), .x2(x2), .x1(x1), .x0(x0), .f(systematyczne_f_1_f));
  heurystyczne_g heurystyczne_g_1 (.x3(x3), .x2(x2), .x1(x1), .x0(x0), .g(heurystyczne_g_1_g));
  _7_Segment_Display u_7_segment_display_1 (
    .g(heurystyczne_g_1_g), .f(systematyczne_f_1_f), .a(heurystyczne_a_1_a), .b(karnaugh_dla_1_sop_b_1_b),
    .e(systematyczne_e_1_out_5), .d(karnaugh_dla_0_pos_d_1_d), .c(karnaugh_dla_0_pos_c_1_c));  // open: dp
endmodule

module karnaugh_dla_1_SOP_b (
  input  x3,
  input  x2,
  input  x1,
  input  x0,
  output b
);

  wire and_1_out, and_2_out, not_1_out, not_2_out, not_3_out;

  not not_1 (not_1_out, x2);
  not not_2 (not_2_out, x1);
  not not_3 (not_3_out, x0);
  and and_1 (and_1_out, not_2_out, not_3_out);
  and and_2 (and_2_out, x1, x0);
  or or_1 (b, not_1_out, and_1_out, and_2_out);
endmodule

module karnaugh_dla_0_POS_d (
  input  x3,
  input  x2,
  input  x1,
  input  x0,
  output d
);

  wire not_1_out, not_2_out, not_3_out, or_1_out, or_2_out, or_3_out;

  not not_1 (not_1_out, x2);
  not not_2 (not_2_out, x1);
  not not_3 (not_3_out, x0);
  or or_1 (or_1_out, x3, x2, x1, not_3_out);
  or or_2 (or_2_out, not_1_out, x1, x0);
  or or_3 (or_3_out, x3, not_1_out, not_2_out, not_3_out);
  and and_1 (d, or_1_out, or_2_out, or_3_out);
endmodule

module karnaugh_dla_0_POS_c (
  input  x3,
  input  x2,
  input  x1,
  input  x0,
  output c
);

  wire not_1_out;

  not not_1 (not_1_out, x1);
  or or_1 (c, x2, not_1_out, x0);
endmodule
